# Fritzing sketch Circuito_Arduino_Bluetooth_Relays (saved by Fritzing 0.9.3b)
breadboards: 1

parts:
  Componente1 = Arduino Uno (Rev3)
  Componente3 = Bluetooth HC-05 Macho
  WeMos_D1_Mini_Relay_Shield_V1 = WeMos D1 Mini Relay Shield V2
  WeMos_D1_Mini_Relay_Shield_V2 = WeMos D1 Mini Relay Shield V2
  WeMos_D1_Mini_Relay_Shield_V3 = WeMos D1 Mini Relay Shield V2
  WeMos_D1_Mini_Relay_Shield_V4 = WeMos D1 Mini Relay Shield V2

nets:
  N1: Componente1.D9_PWM, WeMos_D1_Mini_Relay_Shield_V2.D4
  N2: Componente1.D10_PWM/SS, WeMos_D1_Mini_Relay_Shield_V1.D4
  N3: Componente1.D11_PWM/MOSI, WeMos_D1_Mini_Relay_Shield_V4.D4
  N4: Componente1.D12/MISO, WeMos_D1_Mini_Relay_Shield_V3.D4
  N5: Componente1.D0/RX, Componente3.TXD
  N6: Componente1.D1/TX, Componente3.RXD
  5V: Componente1.5V, Componente3.VCC, WeMos_D1_Mini_Relay_Shield_V1.5V, WeMos_D1_Mini_Relay_Shield_V2.5V, WeMos_D1_Mini_Relay_Shield_V3.5V, WeMos_D1_Mini_Relay_Shield_V4.5V
  GND: Componente1.GND, Componente3.GND, WeMos_D1_Mini_Relay_Shield_V1.G, WeMos_D1_Mini_Relay_Shield_V2.G, WeMos_D1_Mini_Relay_Shield_V3.G, WeMos_D1_Mini_Relay_Shield_V4.G
